# Fritzing sketch shield (saved by Fritzing 0.9.9b)
circuit board: 6.5cm x 3.2cm
breadboards: 1

parts:
  LC76G = SUP500F [package=sup500f]
  J4 = female pin header, 4 pins [form="♀ (female)"]
  S1 = Round Pushbutton
  J5 = Piezo Speaker
  J2 = Raspberry Pi Header 40pin [form="♂ (male)" package=THT]

nets:
  N1: LC76G.RX-I, J4.pin3, J2.GIPO14
  N2: LC76G.TX-O, J4.pin2, J2.GIPO15
  GND: LC76G.GND, J4.pin1, S1.leg0, J5.pin1, J2.GND
  VCC: LC76G.VCC, J4.pin4, J2.5V
  N3: S1.leg1, J2.GPIO3
  N4: J5.pin2, J2.GIPO21

notes:
  yellow - RX
  blue - TX
  black - GND
  red - VCC
  TX
  RX
  GND
  VCC
  PWR_BTN
  piezo
  github.com/
  jsfraz/trek-tracker
  LC76G
  Fritzing did't have this exact part :)

custom parts:
  Raspberry Pi Header 40pin: Raspberry Pi 40 pin header - for creating your own shields.
